// Logisim project 2nmod5.circ as structural Verilog: 3 circuits, main circuit mod5
module mod5 (
  input  In,
  output S0,
  output S1,
  output S2,
  output S3,
  output S4
);

  wire Clk, nextlogic_1_s0_new, nextlogic_1_s1_new, s0_t, s1_t;

  Clock clock_1 (.out(Clk));
  nextLogic nextlogic_1 (.s1(s1_t), .s0(s0_t), .In(In), .s1_new(nextlogic_1_s1_new), .s0_new(nextlogic_1_s0_new));
  Register #(.width(1)) State0 (.D(nextlogic_1_s0_new), .Q(s0_t), .clk(Clk));  // open: en, clr
  Register #(.width(1)) State1 (.D(nextlogic_1_s1_new), .Q(s1_t), .clk(Clk));  // open: en, clr
  outputLogic outputlogic_1 (.state1(s1_t), .state0(s0_t), .in(In), .s0(S0), .s1(S1), .s2(S2), .s3(S3), .s4(S4));
endmodule

module nextLogic (
  input  s1,
  input  s0,
  input  In,
  output s1_new,
  output s0_new
);


  assign s0_new = In;
  assign s1_new = s0;
endmodule

module outputLogic (
  input  state1,
  input  state0,
  input  in,
  output s0,
  output s1,
  output s2,
  output s3,
  output s4
);

  wire not_1_out, not_2_out, not_3_out, not_4_out;

  not not_1 (not_1_out, state0);
  not not_2 (not_2_out, in);
  not not_3 (not_3_out, state0);
  and and_1 (s3, state0, in);
  not not_4 (not_4_out, in);
  and and_2 (s1, not_1_out, not_2_out);
  and and_3 (s2, not_3_out, in);
  and and_4 (s4, state0, not_4_out);

  assign s0 = 1'b0;
endmodule
