// Logisim project fibonacci1.circ as structural Verilog: 1 circuit, main circuit main
module main (
  input  [2:0] N,
  output [3:0] Ans
);

  wire clk, comparator_1_lt, \initial ;
  wire [3:0] adder_1_out, bit_extender_1_out, counter_2_q, Fn_2_q, multiplexer_1_out, multiplexer_2_out, Out,
       sum;

  Clock clock_1 (.out(clk));
  Counter #(.width(1), .max('h1), .ongoal("stay")) counter_1 (
    .Q(\initial ), .clk(clk));  // open: load, D, count, carry, clr
  Counter #(.width(4), .max('hf), .ongoal("stay")) counter_2 (
    .Q(counter_2_q), .clk(clk));  // open: load, D, count, carry, clr
  Multiplexer #(.width(4)) multiplexer_1 (
    .in0(4'b0001), .in1(sum), .out(multiplexer_1_out), .sel(\initial ));  // open: en
  Multiplexer #(.width(4)) multiplexer_2 (
    .in0(4'b0000), .in1(Out), .out(multiplexer_2_out), .sel(\initial ));  // open: en
  assign bit_extender_1_out = {{1{1'b0}}, N};  // Bit_Extender bit_extender_1
  Adder #(.width(4)) adder_1 (.a(4'b0001), .b(counter_2_q), .out(adder_1_out));  // open: cin, cout
  Register #(.width(4)) Fn_1 (.D(multiplexer_1_out), .Q(Out), .clk(clk));  // open: en, clr
  Register #(.width(4)) Fn_2 (.D(multiplexer_2_out), .Q(Fn_2_q), .clk(clk));  // open: en, clr
  Comparator #(.width(4), .mode("unsigned")) comparator_1 (
    .a(bit_extender_1_out), .b(adder_1_out), .lt(comparator_1_lt));  // open: gt, eq
  Adder #(.width(4)) adder_2 (.a(Out), .b(Fn_2_q), .out(sum));  // open: cin, cout
  Register #(.width(4)) \output  (.D(Out), .Q(Ans), .clk(comparator_1_lt));  // open: en, clr

  // Other names for the same wires on the sheet: in[2:0] = N
endmodule
