// Logisim project CRC.circ as structural Verilog: 2 circuits, main circuit CRC
module CRC (
  input  [7:0] \被除数A ,
  input  [3:0] \除数B ,
  output [10:0] out_3
);

  wire [0:0] crc;
  wire [3:0] n4bit_mod2_1_out, n4bit_mod2_2_out, n4bit_mod2_3_out, n4bit_mod2_4_out, n4bit_mod2_5_out,
       n4bit_mod2_6_out, n4bit_mod2_7_out;

  _4bit_mod2 u_4bit_mod2_1 (.nextBit(\被除数A [3]), .\被除数 (\被除数A [7:4]), .\除数 (\除数B ), .out(n4bit_mod2_1_out));
  _4bit_mod2 u_4bit_mod2_2 (.nextBit(\被除数A [2]), .\被除数 (n4bit_mod2_1_out), .\除数 (\除数B ), .out(n4bit_mod2_2_out));
  _4bit_mod2 u_4bit_mod2_3 (.nextBit(\被除数A [1]), .\被除数 (n4bit_mod2_2_out), .\除数 (\除数B ), .out(n4bit_mod2_3_out));
  _4bit_mod2 u_4bit_mod2_4 (.nextBit(\被除数A [0]), .\被除数 (n4bit_mod2_3_out), .\除数 (\除数B ), .out(n4bit_mod2_4_out));
  _4bit_mod2 u_4bit_mod2_5 (.nextBit(1'b0), .\被除数 (n4bit_mod2_4_out), .\除数 (\除数B ), .out(n4bit_mod2_5_out));
  _4bit_mod2 u_4bit_mod2_6 (.nextBit(1'b0), .\被除数 (n4bit_mod2_5_out), .\除数 (\除数B ), .out(n4bit_mod2_6_out));
  _4bit_mod2 u_4bit_mod2_7 (.nextBit(1'b0), .\被除数 (n4bit_mod2_6_out), .\除数 (\除数B ), .out(n4bit_mod2_7_out));
  _4bit_mod2 u_4bit_mod2_8 (.nextBit(1'b0), .\被除数 (n4bit_mod2_7_out), .\除数 (\除数B ), .out({out_3[2:0], crc[0]}));

  assign out_3[10:3] = \被除数A ;

  // Other names for the same wires on the sheet: B[3:0] = \除数B ; crc[3:1] = out_3[2:0]; A[10:3] = \被除数A 
endmodule

// Mod2
module _4bit_mod2 (
  input  nextBit,
  input  [3:0] \被除数 ,
  input  [3:0] \除数 ,
  output [3:0] out
);

  wire [3:0] multiplexer_1_out;
  wire [3:3] xor_1_out;

  Multiplexer #(.width(4)) multiplexer_1 (
    .in0(4'b0000), .in1(\除数 ), .out(multiplexer_1_out), .sel(\被除数 [3]));  // open: en
  assign {xor_1_out[3], out[3:1]} = \被除数  ^ multiplexer_1_out;  // XOR_Gate xor_1, 4 bits wide

  assign out[0] = nextBit;
endmodule
