// Logisim project GRF.circ as structural Verilog: 2 circuits, main circuit grf
module grf (
  input  in_1,
  input  in_2,
  input  in_3,
  input  [4:0] in_4,
  input  [4:0] in_5,
  input  [4:0] in_6,
  input  [31:0] in_7,
  output [31:0] out_8,
  output [31:0] out_9
);

  // GRF grf_1: pin names not known; wires that end beside it: in_4, in_5, in_6, in_7, in_1, in_2, in_3, out_8, out_9
endmodule

module GRF (
  input  Clk,
  input  Reset,
  input  WE,
  input  [4:0] A1,
  input  [4:0] A2,
  input  [4:0] A3,
  input  [31:0] WD,
  output [31:0] RD1,
  output [31:0] RD2
);

  wire [31:0] demultiplexer_1_out0, demultiplexer_1_out1, demultiplexer_1_out2, demultiplexer_1_out3,
       demultiplexer_1_out4, demultiplexer_1_out5, demultiplexer_1_out6, demultiplexer_1_out7,
       demultiplexer_2_out1, demultiplexer_2_out2, demultiplexer_2_out3, demultiplexer_3_out0,
       demultiplexer_3_out1, demultiplexer_3_out2, demultiplexer_3_out3, demultiplexer_4_out0,
       demultiplexer_4_out1, demultiplexer_4_out2, demultiplexer_4_out3, demultiplexer_5_out0,
       demultiplexer_5_out1, demultiplexer_5_out2, demultiplexer_5_out3, demultiplexer_6_out0,
       demultiplexer_6_out1, demultiplexer_6_out2, demultiplexer_6_out3, demultiplexer_7_out0,
       demultiplexer_7_out1, demultiplexer_7_out2, demultiplexer_7_out3, demultiplexer_8_out0,
       demultiplexer_8_out1, demultiplexer_8_out2, demultiplexer_8_out3, demultiplexer_9_out0,
       demultiplexer_9_out1, demultiplexer_9_out2, demultiplexer_9_out3, multiplexer_1_out,
       multiplexer_2_out, multiplexer_3_out, multiplexer_4_out, multiplexer_5_out, multiplexer_6_out,
       multiplexer_7_out, multiplexer_8_out, multiplexer_10_out, multiplexer_11_out, multiplexer_12_out,
       multiplexer_13_out, multiplexer_14_out, multiplexer_15_out, multiplexer_16_out, multiplexer_17_out,
       register_1_q, register_2_q, register_3_q, register_4_q, register_5_q, register_6_q, register_7_q,
       register_8_q, register_9_q, register_10_q, register_11_q, register_12_q, register_13_q, register_14_q,
       register_15_q, register_16_q, register_17_q, register_18_q, register_19_q, register_20_q,
       register_21_q, register_22_q, register_23_q, register_24_q, register_25_q, register_26_q,
       register_27_q, register_28_q, register_29_q, register_30_q, register_31_q, register_32_q;

  Demultiplexer #(.select(3), .width(32), .tristate("true")) demultiplexer_1 (
    .out0(demultiplexer_1_out0), .out1(demultiplexer_1_out1), .out2(demultiplexer_1_out2),
    .out3(demultiplexer_1_out3), .out4(demultiplexer_1_out4), .out5(demultiplexer_1_out5),
    .out6(demultiplexer_1_out6), .out7(demultiplexer_1_out7), .in(WD), .sel(A3[2:0]));  // open: en
  Demultiplexer #(.select(2), .width(32), .tristate("true")) demultiplexer_2 (
    .out1(demultiplexer_2_out1), .out2(demultiplexer_2_out2), .out3(demultiplexer_2_out3),
    .in(demultiplexer_1_out0), .sel(A3[4:3]));  // open: out0, en
  Demultiplexer #(.select(2), .width(32), .tristate("true")) demultiplexer_3 (
    .out0(demultiplexer_3_out0), .out1(demultiplexer_3_out1), .out2(demultiplexer_3_out2),
    .out3(demultiplexer_3_out3), .in(demultiplexer_1_out1), .sel(A3[4:3]));  // open: en
  Demultiplexer #(.select(2), .width(32), .tristate("true")) demultiplexer_4 (
    .out0(demultiplexer_4_out0), .out1(demultiplexer_4_out1), .out2(demultiplexer_4_out2),
    .out3(demultiplexer_4_out3), .in(demultiplexer_1_out2), .sel(A3[4:3]));  // open: en
  Demultiplexer #(.select(2), .width(32), .tristate("true")) demultiplexer_5 (
    .out0(demultiplexer_5_out0), .out1(demultiplexer_5_out1), .out2(demultiplexer_5_out2),
    .out3(demultiplexer_5_out3), .in(demultiplexer_1_out3), .sel(A3[4:3]));  // open: en
  Demultiplexer #(.select(2), .width(32), .tristate("true")) demultiplexer_6 (
    .out0(demultiplexer_6_out0), .out1(demultiplexer_6_out1), .out2(demultiplexer_6_out2),
    .out3(demultiplexer_6_out3), .in(demultiplexer_1_out4), .sel(A3[4:3]));  // open: en
  Demultiplexer #(.select(2), .width(32), .tristate("true")) demultiplexer_7 (
    .out0(demultiplexer_7_out0), .out1(demultiplexer_7_out1), .out2(demultiplexer_7_out2),
    .out3(demultiplexer_7_out3), .in(demultiplexer_1_out5), .sel(A3[4:3]));  // open: en
  Demultiplexer #(.select(2), .width(32), .tristate("true")) demultiplexer_8 (
    .out0(demultiplexer_8_out0), .out1(demultiplexer_8_out1), .out2(demultiplexer_8_out2),
    .out3(demultiplexer_8_out3), .in(demultiplexer_1_out6), .sel(A3[4:3]));  // open: en
  Demultiplexer #(.select(2), .width(32), .tristate("true")) demultiplexer_9 (
    .out0(demultiplexer_9_out0), .out1(demultiplexer_9_out1), .out2(demultiplexer_9_out2),
    .out3(demultiplexer_9_out3), .in(demultiplexer_1_out7), .sel(A3[4:3]));  // open: en
  Register #(.width(32)) register_1 (.en(WE), .Q(register_1_q), .clk(Clk), .clr(Reset));  // open: D
  Register #(.width(32)) register_2 (.D(demultiplexer_3_out0), .en(WE), .Q(register_2_q), .clk(Clk), .clr(Reset));
  Register #(.width(32)) register_3 (.D(demultiplexer_4_out0), .en(WE), .Q(register_3_q), .clk(Clk), .clr(Reset));
  Register #(.width(32)) register_4 (.D(demultiplexer_5_out0), .en(WE), .Q(register_4_q), .clk(Clk), .clr(Reset));
  Register #(.width(32)) register_5 (.D(demultiplexer_6_out0), .en(WE), .Q(register_5_q), .clk(Clk), .clr(Reset));
  Register #(.width(32)) register_6 (.D(demultiplexer_7_out0), .en(WE), .Q(register_6_q), .clk(Clk), .clr(Reset));
  Register #(.width(32)) register_7 (.D(demultiplexer_8_out0), .en(WE), .Q(register_7_q), .clk(Clk), .clr(Reset));
  Register #(.width(32)) register_8 (.D(demultiplexer_9_out0), .en(WE), .Q(register_8_q), .clk(Clk), .clr(Reset));
  Register #(.width(32)) register_9 (.D(demultiplexer_2_out1), .en(WE), .Q(register_9_q), .clk(Clk), .clr(Reset));
  Register #(.width(32)) register_10 (.D(demultiplexer_3_out1), .en(WE), .Q(register_10_q), .clk(Clk), .clr(Reset));
  Register #(.width(32)) register_11 (.D(demultiplexer_4_out1), .en(WE), .Q(register_11_q), .clk(Clk), .clr(Reset));
  Register #(.width(32)) register_12 (.D(demultiplexer_5_out1), .en(WE), .Q(register_12_q), .clk(Clk), .clr(Reset));
  Register #(.width(32)) register_13 (.D(demultiplexer_6_out1), .en(WE), .Q(register_13_q), .clk(Clk), .clr(Reset));
  Register #(.width(32)) register_14 (.D(demultiplexer_7_out1), .en(WE), .Q(register_14_q), .clk(Clk), .clr(Reset));
  Register #(.width(32)) register_15 (.D(demultiplexer_8_out1), .en(WE), .Q(register_15_q), .clk(Clk), .clr(Reset));
  Register #(.width(32)) register_16 (.D(demultiplexer_9_out1), .en(WE), .Q(register_16_q), .clk(Clk), .clr(Reset));
  Register #(.width(32)) register_17 (.D(demultiplexer_2_out2), .en(WE), .Q(register_17_q), .clk(Clk), .clr(Reset));
  Register #(.width(32)) register_18 (.D(demultiplexer_3_out2), .en(WE), .Q(register_18_q), .clk(Clk), .clr(Reset));
  Register #(.width(32)) register_19 (.D(demultiplexer_4_out2), .en(WE), .Q(register_19_q), .clk(Clk), .clr(Reset));
  Register #(.width(32)) register_20 (.D(demultiplexer_5_out2), .en(WE), .Q(register_20_q), .clk(Clk), .clr(Reset));
  Register #(.width(32)) register_21 (.D(demultiplexer_6_out2), .en(WE), .Q(register_21_q), .clk(Clk), .clr(Reset));
  Register #(.width(32)) register_22 (.D(demultiplexer_7_out2), .en(WE), .Q(register_22_q), .clk(Clk), .clr(Reset));
  Register #(.width(32)) register_23 (.D(demultiplexer_8_out2), .en(WE), .Q(register_23_q), .clk(Clk), .clr(Reset));
  Register #(.width(32)) register_24 (.D(demultiplexer_9_out2), .en(WE), .Q(register_24_q), .clk(Clk), .clr(Reset));
  Register #(.width(32)) register_25 (.D(demultiplexer_2_out3), .en(WE), .Q(register_25_q), .clk(Clk), .clr(Reset));
  Register #(.width(32)) register_26 (.D(demultiplexer_3_out3), .en(WE), .Q(register_26_q), .clk(Clk), .clr(Reset));
  Register #(.width(32)) register_27 (.D(demultiplexer_4_out3), .en(WE), .Q(register_27_q), .clk(Clk), .clr(Reset));
  Register #(.width(32)) register_28 (.D(demultiplexer_5_out3), .en(WE), .Q(register_28_q), .clk(Clk), .clr(Reset));
  Register #(.width(32)) register_29 (.D(demultiplexer_6_out3), .en(WE), .Q(register_29_q), .clk(Clk), .clr(Reset));
  Register #(.width(32)) register_30 (.D(demultiplexer_7_out3), .en(WE), .Q(register_30_q), .clk(Clk), .clr(Reset));
  Register #(.width(32)) register_31 (.D(demultiplexer_8_out3), .en(WE), .Q(register_31_q), .clk(Clk), .clr(Reset));
  Register #(.width(32)) register_32 (.D(demultiplexer_9_out3), .en(WE), .Q(register_32_q), .clk(Clk), .clr(Reset));
  Multiplexer #(.select(2), .width(32)) multiplexer_1 (
    .in0(register_1_q), .in1(register_9_q), .in2(register_17_q), .in3(register_25_q),
    .out(multiplexer_1_out), .sel(A1[4:3]));  // open: en
  Multiplexer #(.select(2), .width(32)) multiplexer_2 (
    .in0(register_2_q), .in1(register_10_q), .in2(register_18_q), .in3(register_26_q),
    .out(multiplexer_2_out), .sel(A1[4:3]));  // open: en
  Multiplexer #(.select(2), .width(32)) multiplexer_3 (
    .in0(register_3_q), .in1(register_11_q), .in2(register_19_q), .in3(register_27_q),
    .out(multiplexer_3_out), .sel(A1[4:3]));  // open: en
  Multiplexer #(.select(2), .width(32)) multiplexer_4 (
    .in0(register_4_q), .in1(register_12_q), .in2(register_20_q), .in3(register_28_q),
    .out(multiplexer_4_out), .sel(A1[4:3]));  // open: en
  Multiplexer #(.select(2), .width(32)) multiplexer_5 (
    .in0(register_5_q), .in1(register_13_q), .in2(register_21_q), .in3(register_29_q),
    .out(multiplexer_5_out), .sel(A1[4:3]));  // open: en
  Multiplexer #(.select(2), .width(32)) multiplexer_6 (
    .in0(register_6_q), .in1(register_14_q), .in2(register_22_q), .in3(register_30_q),
    .out(multiplexer_6_out), .sel(A1[4:3]));  // open: en
  Multiplexer #(.select(2), .width(32)) multiplexer_7 (
    .in0(register_7_q), .in1(register_15_q), .in2(register_23_q), .in3(register_31_q),
    .out(multiplexer_7_out), .sel(A1[4:3]));  // open: en
  Multiplexer #(.select(2), .width(32)) multiplexer_8 (
    .in0(register_8_q), .in1(register_16_q), .in2(register_24_q), .in3(register_32_q),
    .out(multiplexer_8_out), .sel(A1[4:3]));  // open: en
  Multiplexer #(.select(3), .width(32)) multiplexer_9 (
    .in0(multiplexer_1_out), .in1(multiplexer_2_out), .in2(multiplexer_3_out), .in3(multiplexer_4_out),
    .in4(multiplexer_5_out), .in5(multiplexer_6_out), .in6(multiplexer_7_out), .in7(multiplexer_8_out),
    .out(RD1), .sel(A1[2:0]));  // open: en
  Multiplexer #(.select(2), .width(32)) multiplexer_10 (
    .in0(register_3_q), .in1(register_11_q), .in2(register_19_q), .in3(register_27_q),
    .out(multiplexer_10_out), .sel(A2[4:3]));  // open: en
  Multiplexer #(.select(2), .width(32)) multiplexer_11 (
    .in0(register_4_q), .in1(register_12_q), .in2(register_20_q), .in3(register_28_q),
    .out(multiplexer_11_out), .sel(A2[4:3]));  // open: en
  Multiplexer #(.select(2), .width(32)) multiplexer_12 (
    .in0(register_5_q), .in1(register_13_q), .in2(register_21_q), .in3(register_29_q),
    .out(multiplexer_12_out), .sel(A2[4:3]));  // open: en
  Multiplexer #(.select(2), .width(32)) multiplexer_13 (
    .in0(register_6_q), .in1(register_14_q), .in2(register_22_q), .in3(register_30_q),
    .out(multiplexer_13_out), .sel(A2[4:3]));  // open: en
  Multiplexer #(.select(2), .width(32)) multiplexer_14 (
    .in0(register_7_q), .in1(register_15_q), .in2(register_23_q), .in3(register_31_q),
    .out(multiplexer_14_out), .sel(A2[4:3]));  // open: en
  Multiplexer #(.select(2), .width(32)) multiplexer_15 (
    .in0(register_8_q), .in1(register_16_q), .in2(register_24_q), .in3(register_32_q),
    .out(multiplexer_15_out), .sel(A2[4:3]));  // open: en
  Multiplexer #(.select(2), .width(32)) multiplexer_16 (
    .in0(register_1_q), .in1(register_9_q), .in2(register_17_q), .in3(register_25_q),
    .out(multiplexer_16_out), .sel(A2[4:3]));  // open: en
  Multiplexer #(.select(2), .width(32)) multiplexer_17 (
    .in0(register_2_q), .in1(register_10_q), .in2(register_18_q), .in3(register_26_q),
    .out(multiplexer_17_out), .sel(A2[4:3]));  // open: en
  Multiplexer #(.select(3), .width(32)) multiplexer_18 (
    .in0(multiplexer_16_out), .in1(multiplexer_17_out), .in2(multiplexer_10_out), .in3(multiplexer_11_out),
    .in4(multiplexer_12_out), .in5(multiplexer_13_out), .in6(multiplexer_14_out), .in7(multiplexer_15_out),
    .out(RD2), .sel(A2[2:0]));  // open: en

  // Other names for the same wires on the sheet: A1_low[2:0] = A1[2:0]; A1_high[1:0] = A1[4:3]; A2_low[2:0] = A2[2:0];
  //   A2_high[1:0] = A2[4:3]; A3_low[2:0] = A3[2:0]; A3_high[1:0] = A3[4:3]
endmodule
