// Logisim project Navigation.circ as structural Verilog: 4 circuits, main circuit navigation
module navigation (
  input  [1:0] dir,
  input  in_2,
  input  in_3,
  output arrive,
  output hit
);

  wire nextstate1_1_s0_new, nextstate1_1_s1_new, nextstate1_1_s2_new, nextstatelogic2_1_dir, s0, s1, s2;

  nextstate1 nextstate1_1 (
    .s2(s2), .s1(s1), .s2_new(nextstate1_1_s2_new), .s0(s0), .in1(dir[1]), .in0(dir[0]),
    .s1_new(nextstate1_1_s1_new), .s0_new(nextstate1_1_s0_new));
  nextStateLogic2 nextstatelogic2_1 (
    .s2(s2), .s1(s1), .s0(s0), .in1(dir[1]), .in0(dir[0]), .dir(nextstatelogic2_1_dir));
  Register #(.width(1)) where2 (.D(nextstate1_1_s2_new), .Q(s2), .clk(in_2), .clr(in_3));  // open: en
  Register #(.width(1)) where1 (.D(nextstate1_1_s1_new), .Q(s1), .clk(in_2), .clr(in_3));  // open: en
  Register #(.width(1)) where0 (.D(nextstate1_1_s0_new), .Q(s0), .clk(in_2), .clr(in_3));  // open: en
  Register #(.width(1)) u_hit (.D(nextstatelogic2_1_dir), .Q(hit), .clk(in_2), .clr(in_3));  // open: en
  outPut1 output1_1 (.s2(s2), .s1(s1), .s0(s0), .arrive(arrive));

  // Other names for the same wires on the sheet: clk = in_2; reset = in_3
endmodule

module nextstate1 (
  input  s2,
  input  s1,
  input  s0,
  input  in1,
  input  in0,
  output s2_new,
  output s1_new,
  output s0_new
);

  wire and_1_out, and_2_out, and_3_out, and_4_out, and_5_out, and_6_out, and_7_out, and_8_out, and_9_out,
       and_10_out, and_11_out, and_12_out, not_1_out, not_2_out, not_3_out, not_4_out, not_5_out, not_6_out,
       not_7_out, not_8_out, not_9_out, not_10_out, not_11_out, not_12_out, not_13_out, not_14_out,
       not_15_out, not_16_out, not_17_out, not_18_out, not_19_out;

  not not_1 (not_1_out, s0);
  not not_2 (not_2_out, in1);
  not not_3 (not_3_out, in0);
  not not_4 (not_4_out, in1);
  not not_5 (not_5_out, s1);
  not not_6 (not_6_out, in1);
  not not_7 (not_7_out, in1);
  not not_8 (not_8_out, in0);
  not not_9 (not_9_out, s0);
  not not_10 (not_10_out, in1);
  not not_11 (not_11_out, s0);
  not not_12 (not_12_out, in0);
  not not_13 (not_13_out, s2);
  not not_14 (not_14_out, s1);
  not not_15 (not_15_out, in1);
  not not_16 (not_16_out, in0);
  not not_17 (not_17_out, in1);
  not not_18 (not_18_out, in0);
  not not_19 (not_19_out, in0);
  and and_1 (and_1_out, s1, not_1_out, not_2_out, not_3_out);
  and and_2 (and_2_out, s1, s0, not_4_out, in0);
  and and_3 (and_3_out, not_5_out, s0, not_6_out);
  and and_4 (and_4_out, s0, not_7_out, not_8_out);
  and and_5 (and_5_out, s1, not_9_out, not_10_out, in0);
  and and_6 (and_6_out, s1, not_11_out, in1, not_12_out);
  and and_7 (and_7_out, s1, s0, in1, in0);
  and and_8 (and_8_out, not_13_out, not_14_out, not_15_out, not_16_out);
  and and_9 (and_9_out, s0, not_17_out, not_18_out);
  and and_10 (and_10_out, s0, in1, in0);
  and and_11 (and_11_out, s1, in1, in0);
  and and_12 (and_12_out, s1, s0, not_19_out);
  or or_1 (s2_new, and_1_out, and_2_out);
  or or_2 (s1_new, and_3_out, and_4_out, and_5_out, and_6_out, and_7_out);
  or or_3 (s0_new, and_8_out, and_9_out, and_10_out, and_11_out, and_12_out);
endmodule

module outPut1 (
  input  s2,
  input  s1,
  input  s0,
  output arrive
);

  wire not_1_out, not_2_out;

  not not_1 (not_1_out, s1);
  not not_2 (not_2_out, s0);
  and and_1 (arrive, s2, not_1_out, not_2_out);
endmodule

module nextStateLogic2 (
  input  s2,
  input  s1,
  input  s0,
  input  in1,
  input  in0,
  output dir
);

  wire and_1_out, and_2_out, and_3_out, and_4_out, and_5_out, not_1_out, not_2_out, not_3_out, not_4_out,
       not_5_out, not_6_out, not_7_out, not_8_out, not_9_out, not_10_out, not_11_out, not_12_out;

  not not_1 (not_1_out, s2);
  not not_2 (not_2_out, s0);
  not not_3 (not_3_out, in1);
  not not_4 (not_4_out, s2);
  not not_5 (not_5_out, s0);
  not not_6 (not_6_out, in0);
  not not_7 (not_7_out, s2);
  not not_8 (not_8_out, s1);
  not not_9 (not_9_out, s2);
  not not_10 (not_10_out, s2);
  not not_11 (not_11_out, in1);
  not not_12 (not_12_out, in0);
  and and_1 (and_1_out, not_1_out, not_2_out, not_3_out, in0);
  and and_2 (and_2_out, not_4_out, not_5_out, in1, not_6_out);
  and and_3 (and_3_out, not_7_out, not_8_out, in1, in0);
  and and_4 (and_4_out, not_9_out, s0, in1, in0);
  and and_5 (and_5_out, not_10_out, s1, s0, not_11_out, not_12_out);
  or or_1 (dir, and_1_out, and_2_out, and_3_out, and_4_out, and_5_out);
endmodule
