// Logisim project Q4_fsm.circ as structural Verilog: 3 circuits, main circuit fsm
module fsm (
  input  clr,
  input  [1:0] in,
  output out_3
);

  wire and_1_out, and_2_out, and_3_out, clock_1_out, clr_t, nextstate_1_s0_new, nextstate_1_s1_new,
       nextstate_1_s2_new, s0, s1, s2;

  not not_1 (clr_t, clr);
  nextState nextstate_1 (
    .s2(s2), .s1(s1), .s0(s0), .s2_new(nextstate_1_s2_new), .in1(in[1]), .in0(in[0]),
    .s1_new(nextstate_1_s1_new), .s0_new(nextstate_1_s0_new));
  and and_1 (and_1_out, clr_t, nextstate_1_s2_new);
  Register #(.width(1)) u_s2 (.D(and_1_out), .Q(s2), .clk(clock_1_out));  // open: en, clr
  and and_2 (and_2_out, clr_t, nextstate_1_s1_new);
  Register #(.width(1)) u_s1 (.D(and_2_out), .Q(s1), .clk(clock_1_out));  // open: en, clr
  Register #(.width(1)) u_s0 (.D(and_3_out), .Q(s0), .clk(clock_1_out));  // open: en, clr
  and and_3 (and_3_out, nextstate_1_s0_new, clr_t);
  Clock clock_1 (.out(clock_1_out));
  outputLogic outputlogic_1 (.s2(s2), .s1(s1), .s0(s0), .in1(in[1]), .in0(in[0]), .out(out_3));
endmodule

module nextState (
  input  s2,
  input  s1,
  input  s0,
  input  in1,
  input  in0,
  output s2_new,
  output s1_new,
  output s0_new
);

  wire and_1_out, and_2_out, and_3_out, and_4_out, and_5_out, and_6_out, and_7_out, and_8_out, and_9_out,
       and_10_out, and_11_out, and_12_out, and_13_out, not_1_out, not_2_out, not_3_out, not_4_out, not_5_out,
       not_6_out, not_7_out, not_8_out, not_9_out, not_10_out, not_11_out, not_12_out, not_13_out,
       not_14_out, not_15_out, not_16_out, not_17_out, not_18_out, not_19_out, not_20_out, not_21_out,
       not_22_out, not_23_out, not_24_out;

  not not_1 (not_1_out, in0);
  not not_2 (not_2_out, s2);
  not not_3 (not_3_out, in0);
  not not_4 (not_4_out, in0);
  not not_5 (not_5_out, in0);
  not not_6 (not_6_out, s2);
  not not_7 (not_7_out, s1);
  not not_8 (not_8_out, in1);
  not not_9 (not_9_out, s2);
  not not_10 (not_10_out, s0);
  not not_11 (not_11_out, in1);
  not not_12 (not_12_out, in0);
  not not_13 (not_13_out, in0);
  not not_14 (not_14_out, in0);
  not not_15 (not_15_out, s0);
  not not_16 (not_16_out, in1);
  not not_17 (not_17_out, s2);
  not not_18 (not_18_out, s1);
  not not_19 (not_19_out, in0);
  not not_20 (not_20_out, s2);
  not not_21 (not_21_out, s0);
  not not_22 (not_22_out, in0);
  not not_23 (not_23_out, in1);
  not not_24 (not_24_out, in1);
  and and_1 (and_1_out, s0, in1, not_1_out);
  and and_2 (and_2_out, not_2_out, s1, in1, not_3_out);
  and and_3 (and_3_out, s1, s0, not_4_out);
  and and_4 (and_4_out, s2, s0, not_5_out);
  and and_5 (and_5_out, not_6_out, not_7_out, s0, not_8_out);
  and and_6 (and_6_out, not_9_out, s1, not_10_out, not_11_out, not_12_out);
  and and_7 (and_7_out, s1, s0, in1, not_13_out);
  and and_8 (and_8_out, s2, s0, in1, not_14_out);
  and and_9 (and_9_out, not_15_out, not_16_out, in0);
  and and_10 (and_10_out, not_17_out, not_18_out, s0, not_19_out);
  and and_11 (and_11_out, not_20_out, s1, not_21_out, not_22_out);
  and and_12 (and_12_out, s1, not_23_out, in0);
  and and_13 (and_13_out, s2, not_24_out, in0);
  or or_1 (s2_new, and_1_out, and_2_out, and_3_out, and_4_out);
  or or_2 (s1_new, and_5_out, and_6_out, and_7_out, and_8_out);
  or or_3 (s0_new, and_9_out, and_10_out, and_11_out, and_12_out, and_13_out);
endmodule

module outputLogic (
  input  s2,
  input  s1,
  input  s0,
  input  in1,
  input  in0,
  output out
);

  wire and_1_out, and_2_out, not_1_out, not_2_out, not_3_out, not_4_out;

  not not_1 (not_1_out, s2);
  not not_2 (not_2_out, in0);
  not not_3 (not_3_out, s1);
  not not_4 (not_4_out, in0);
  and and_1 (and_1_out, not_1_out, s1, s0, not_2_out);
  and and_2 (and_2_out, s2, not_3_out, s0, not_4_out);
  or or_1 (out, and_1_out, and_2_out);
endmodule
