// Logisim project ftoi.circ as structural Verilog: 5 circuits, main circuit ftoi
module ftoi (
  input  [15:0] in_1,
  output [31:0] \int 
);

  wire [1:0] sel;
  wire [4:0] exp_t;
  wire [10:0] Den, Nor;
  wire [31:0] int_1_out, int_2_out;

  assign Den = {{1{1'b0}}, in_1[9:0]};  // Bit_Extender bit_extender_1
  assign Nor = {{1{1'b1}}, in_1[9:0]};  // Bit_Extender bit_extender_2
  \int  int_1 (.sign(in_1[15]), .flaot(Nor), .exp(exp_t), .out(int_1_out));
  \int  int_2 (.sign(in_1[15]), .flaot(Den), .exp(exp_t), .out(int_2_out));
  select select_1 (.Exp(in_1[14:10]), .sel(sel));
  Subtractor #(.width(5)) subtractor_1 (.a(in_1[14:10]), .b(5'b01111), .out(exp_t));  // open: bin, bout
  Multiplexer #(.select(2), .width(32)) multiplexer_1 (
    .in0(int_1_out), .in1(int_2_out), .in2({32{1'b0}}), .in3({32{1'b0}}), .out(\int ), .sel(sel));  // open: en

  // Other names for the same wires on the sheet: frac[9:0] = in_1[9:0]; Exp[4:0] = in_1[14:10]; Sign = in_1[15]
endmodule

module \int  (
  input  sign,
  input  [10:0] flaot,
  input  [4:0] exp,
  output [31:0] out
);

  wire comparator_1_lt;
  wire [30:0] \input , shifter_1_out;
  wire [31:0] multiplexer_1_out, num1, num2;

  assign \input  = {{20{1'b0}}, flaot};  // Bit_Extender bit_extender_1
  Shifter #(.width(31)) shifter_1 (.in(\input ), .\dist (exp), .out(shifter_1_out));
  Multiplexer #(.width(32)) multiplexer_1 (
    .in0(num1), .in1(num2), .out(multiplexer_1_out), .sel(comparator_1_lt));  // open: en
  Comparator #(.width(5)) comparator_1 (.a(exp), .b({5{1'b0}}), .lt(comparator_1_lt));  // open: gt, eq
  getcomple getcomple_1 (.sign(sign), .num({31{1'b0}}), .comple(num2));
  assign out = {{10{multiplexer_1_out[31]}}, multiplexer_1_out[31:10]};  // Bit_Extender bit_extender_2
  getcomple getcomple_2 (.sign(sign), .num({shifter_1_out[30:10], {10{1'b0}}}), .comple(num1));
endmodule

module select (
  input  [4:0] Exp,
  output [1:0] sel
);

  Comparator #(.width(5), .mode("unsigned")) comparator_1 (.a({5{1'b0}}), .b(Exp), .eq(sel[0]));  // open: gt, lt
  Comparator #(.width(5), .mode("unsigned")) comparator_2 (.a(Exp), .b({5{1'b1}}), .eq(sel[1]));  // open: gt, lt
endmodule

module getcomple (
  input  sign,
  input  [30:0] num,
  output [31:0] comple
);

  wire [30:0] xor_1_out;
  wire [31:0] adder_1_out, bit_extender_1_out;

  assign xor_1_out = num ^ {31{1'b1}};  // XOR_Gate xor_1, 31 bits wide
  assign bit_extender_1_out = {{1{1'b0}}, num};  // Bit_Extender bit_extender_1
  Adder #(.width(32)) adder_1 (.a({sign, xor_1_out}), .b(32'h1), .out(adder_1_out));  // open: cin, cout
  Multiplexer #(.width(32)) multiplexer_1 (
    .in0(bit_extender_1_out), .in1(adder_1_out), .out(comple), .sel(sign));  // open: en
endmodule

module test (
  input  [15:0] in_1,
  output [31:0] out_2
);

  ftoi ftoi_1 (.in_1(in_1), .\int (out_2));
endmodule
