// Logisim project fibonacci2.circ as structural Verilog: 6 circuits, main circuit main
module main (
  input  [31:0] N,
  output [31:0] Nth
);

  wire en, Final;
  wire [31:0] n_1_ans;

  n n_1 (.in_1(Final), .ANS(n_1_ans));
  Register #(.width(32)) register_1 (.D(n_1_ans), .Q(Nth), .clk(en));  // open: en, clr
  count count_1 (.IN(N), .out_2(Final), .OUT(en));

  // Other names for the same wires on the sheet: In[31:0] = N
endmodule

// MUL
module \矩阵乘法  (
  input  [31:0] X11,
  input  [31:0] X12,
  input  [31:0] X21,
  input  [31:0] X22,
  input  [31:0] Y11,
  input  [31:0] Y12,
  input  [31:0] Y21,
  input  [31:0] Y22,
  output [31:0] Z11,
  output [31:0] Z12,
  output [31:0] Z21,
  output [31:0] Z22
);

  wire [31:0] multiplier_1_out, multiplier_2_out, multiplier_3_out, multiplier_4_out, multiplier_5_out,
       multiplier_6_out, multiplier_7_out, multiplier_8_out;

  Multiplier #(.width(32)) multiplier_1 (.a(X11), .b(Y11), .out(multiplier_1_out));  // open: cin, cout
  Multiplier #(.width(32)) multiplier_2 (.a(X11), .b(Y12), .out(multiplier_2_out));  // open: cin, cout
  Multiplier #(.width(32)) multiplier_3 (.a(X21), .b(Y11), .out(multiplier_3_out));  // open: cin, cout
  Multiplier #(.width(32)) multiplier_4 (.a(X21), .b(Y12), .out(multiplier_4_out));  // open: cin, cout
  Multiplier #(.width(32)) multiplier_5 (.a(X12), .b(Y21), .out(multiplier_5_out));  // open: cin, cout
  Multiplier #(.width(32)) multiplier_6 (.a(X12), .b(Y22), .out(multiplier_6_out));  // open: cin, cout
  Multiplier #(.width(32)) multiplier_7 (.a(X22), .b(Y21), .out(multiplier_7_out));  // open: cin, cout
  Multiplier #(.width(32)) multiplier_8 (.a(X22), .b(Y22), .out(multiplier_8_out));  // open: cin, cout
  Adder #(.width(32)) adder_1 (.a(multiplier_1_out), .b(multiplier_5_out), .out(Z11));  // open: cin, cout
  Adder #(.width(32)) adder_2 (.a(multiplier_2_out), .b(multiplier_6_out), .out(Z12));  // open: cin, cout
  Adder #(.width(32)) adder_3 (.a(multiplier_3_out), .b(multiplier_7_out), .out(Z21));  // open: cin, cout
  Adder #(.width(32)) adder_4 (.a(multiplier_4_out), .b(multiplier_8_out), .out(Z22));  // open: cin, cout
endmodule

module unitary_matrix (
  output [31:0] X11,
  output [31:0] X12,
  output [31:0] X21,
  output [31:0] X22
);


  assign X11 = 32'h1;
  assign X12 = {32{1'b0}};
  assign X21 = {32{1'b0}};
  assign X22 = 32'h1;
endmodule

module base (
  output [31:0] X11,
  output [31:0] X12,
  output [31:0] X21,
  output [31:0] X22
);


  assign X11 = 32'h1;
  assign X12 = 32'h1;
  assign X21 = 32'h1;
  assign X22 = {32{1'b0}};
endmodule

// COUNT
module count (
  input  [31:0] IN,
  output out_2,
  output OUT
);

  wire CLOCK, comparator_1_eq, not_1_out, or_1_out, TEMP;
  wire [31:0] multiplexer_1_out, NEW, shifter_1_out;

  Shifter #(.width(32), .shift("lr")) shifter_1 (.in(NEW), .\dist (5'b00001), .out(shifter_1_out));
  Clock clock_1 (.out(CLOCK));
  Multiplexer #(.width(32)) multiplexer_1 (
    .in0(IN), .in1(shifter_1_out), .out(multiplexer_1_out), .sel(TEMP));  // open: en
  Bit_Extender #(.in_width(32), .out_width(1)) bit_extender_1 (.in(NEW), .out(out_2));
  Comparator #(.width(32), .mode("unsigned")) comparator_1 (
    .a(NEW), .b({32{1'b0}}), .eq(comparator_1_eq));  // open: gt, lt
  Register #(.width(32)) register_1 (.D(multiplexer_1_out), .Q(NEW), .clk(CLOCK));  // open: en, clr
  Multiplexer multiplexer_2 (.in0(1'b0), .in1(comparator_1_eq), .out(OUT), .sel(TEMP));  // open: en
  not not_1 (not_1_out, CLOCK);
  or or_1 (or_1_out, TEMP, not_1_out);
  Register #(.width(1)) register_2 (.D(or_1_out), .Q(TEMP), .clk(CLOCK));  // open: en, clr
endmodule

module n (
  input  in_1,
  output [31:0] ANS
);

  wire Clock, not_1_out, or_1_out, TMP;
  wire [31:0] a11, a12, a21, a22, b11, b12, b21, b22, be11, be12, be21, be22, c11, c12, c21, c22, g11, g12,
       g21, g22, m11, m12, m21, m22, multiplexer_1_out, multiplexer_2_out, multiplexer_7_out,
       multiplexer_8_out, S11, S21, S22, \矩阵乘法_1_z11 , \矩阵乘法_1_z12 , \矩阵乘法_1_z21 , \矩阵乘法_1_z22 ;

  base base_1 (.X11(a11), .X12(a12), .X21(a21), .X22(a22));
  Multiplexer #(.width(32)) multiplexer_1 (.in0(a11), .in1(c11), .out(multiplexer_1_out), .sel(TMP));  // open: en
  Multiplexer #(.width(32)) multiplexer_2 (.in0(a21), .in1(c21), .out(multiplexer_2_out), .sel(TMP));  // open: en
  Multiplexer #(.width(32)) multiplexer_3 (.in0(m11), .in1(b11), .out(be11), .sel(in_1));  // open: en
  Multiplexer #(.width(32)) multiplexer_4 (.in0(m21), .in1(b21), .out(be21), .sel(in_1));  // open: en
  Multiplexer #(.width(32)) multiplexer_5 (.in0(m11), .in1(S11), .out(g11), .sel(TMP));  // open: en
  Multiplexer #(.width(32)) multiplexer_6 (.in0(m21), .in1(S21), .out(g21), .sel(TMP));  // open: en
  not not_1 (not_1_out, Clock);
  Register #(.width(32)) register_1 (.D(multiplexer_1_out), .Q(b11), .clk(Clock));  // open: en, clr
  Register #(.width(32)) register_2 (.D(multiplexer_2_out), .Q(b21), .clk(Clock));  // open: en, clr
  or or_1 (or_1_out, TMP, not_1_out);
  Register #(.width(1)) register_3 (.D(or_1_out), .Q(TMP), .clk(Clock));  // open: en, clr
  Multiplexer #(.width(32)) multiplexer_7 (.in0(a12), .in1(c12), .out(multiplexer_7_out), .sel(TMP));  // open: en
  Multiplexer #(.width(32)) multiplexer_8 (.in0(a22), .in1(c22), .out(multiplexer_8_out), .sel(TMP));  // open: en
  Multiplexer #(.width(32)) multiplexer_9 (.in0(m12), .in1(b12), .out(be12), .sel(in_1));  // open: en
  Multiplexer #(.width(32)) multiplexer_10 (.in0(m22), .in1(b22), .out(be22), .sel(in_1));  // open: en
  Multiplexer #(.width(32)) multiplexer_11 (.in0(m12), .in1(ANS), .out(g12), .sel(TMP));  // open: en
  Multiplexer #(.width(32)) multiplexer_12 (.in0(m22), .in1(S22), .out(g22), .sel(TMP));  // open: en
  Clock clock_1 (.out(Clock));
  Register #(.width(32)) register_4 (.D(multiplexer_7_out), .Q(b12), .clk(Clock));  // open: en, clr
  Register #(.width(32)) register_5 (.D(multiplexer_8_out), .Q(b22), .clk(Clock));  // open: en, clr
  unitary_matrix unitary_matrix_1 (.X11(m11), .X12(m12), .X21(m21), .X22(m22));
  \矩阵乘法  \u_矩阵乘法_1  (
    .X11(g11), .X12(g12), .X21(g21), .X22(g22), .Y11(be11), .Y12(be12), .Y21(be21), .Y22(be22),
    .Z11(\矩阵乘法_1_z11 ), .Z12(\矩阵乘法_1_z12 ), .Z21(\矩阵乘法_1_z21 ), .Z22(\矩阵乘法_1_z22 ));
  \矩阵乘法  \u_矩阵乘法_2  (
    .X11(b11), .X12(b12), .X21(b21), .X22(b22), .Y11(b11), .Y12(b12), .Y21(b21), .Y22(b22), .Z11(c11),
    .Z12(c12), .Z21(c21), .Z22(c22));
  Register #(.width(32)) register_6 (.D(\矩阵乘法_1_z11 ), .Q(S11), .clk(Clock));  // open: en, clr
  Register #(.width(32)) register_7 (.D(\矩阵乘法_1_z12 ), .Q(ANS), .clk(Clock));  // open: en, clr
  Register #(.width(32)) register_8 (.D(\矩阵乘法_1_z21 ), .Q(S21), .clk(Clock));  // open: en, clr
  Register #(.width(32)) register_9 (.D(\矩阵乘法_1_z22 ), .Q(S22), .clk(Clock));  // open: en, clr

  // Other names for the same wires on the sheet: enter = in_1; S12[31:0] = ANS
endmodule
