// Logisim project latch.circ as structural Verilog: 4 circuits, main circuit SR latch
module SR_latch (
  input  R,
  input  S,
  output Q,
  output nQ
);

  wire or_1_out, or_2_out;

  or or_1 (or_1_out, R, nQ);
  or or_2 (or_2_out, Q, S);
  not not_1 (Q, or_1_out);
  not not_2 (nQ, or_2_out);
endmodule

module SR_latch2 (
  input  in_1,
  input  in_2,
  output out_3,
  output out_4
);

  wire and_1_out, and_2_out, not_1_out, not_2_out;

  not not_1 (not_1_out, in_1);
  not not_2 (not_2_out, in_2);
  and and_1 (and_1_out, not_1_out, out_4);
  not not_3 (out_3, and_1_out);
  not not_4 (out_4, and_2_out);
  and and_2 (and_2_out, out_3, not_2_out);
endmodule

module D_latch (
  input  CLk,
  input  D,
  output out_3,
  output out_4
);

  wire and_1_out, and_2_out, not_1_out;

  and and_1 (and_1_out, CLk, not_1_out);
  not not_1 (not_1_out, D);
  and and_2 (and_2_out, CLk, D);
  SR_latch sr_latch_1 (.R(and_1_out), .S(and_2_out), .Q(out_3), .nQ(out_4));
endmodule

module D_flip_flop (
  input  CLK,
  input  in_2,
  output out_3,
  output out_4
);

  wire d_latch_1_out_3, not_1_out;

  not not_1 (not_1_out, CLK);
  D_latch d_latch_1 (.D(in_2), .CLk(not_1_out), .out_3(d_latch_1_out_3));  // open: out_4
  D_latch d_latch_2 (.D(d_latch_1_out_3), .CLk(CLK), .out_3(out_3), .out_4(out_4));
endmodule
