// Logisim project sort.circ as structural Verilog
module _1bit_swap (
  input  a,
  input  b,
  input  s,
  output out1,
  output out2
);

  wire and_1_out, and_2_out, and_3_out, and_4_out, not_1_out, not_2_out;

  not not_1 (not_1_out, s);
  not not_2 (not_2_out, s);
  and and_1 (and_1_out, b, s);
  and and_2 (and_2_out, a, not_1_out);
  and and_3 (and_3_out, b, not_2_out);
  and and_4 (and_4_out, a, s);
  or or_1 (out1, and_1_out, and_2_out);
  or or_2 (out2, and_3_out, and_4_out);
endmodule

module _4bit_swap (
  input  [3:0] In1,
  input  [3:0] In2,
  input  select,
  output [3:0] OUT1,
  output [3:0] OUT2
);

  _1bit_swap u_1bit_swap_1 (.a(In1[0]), .b(In2[0]), .s(select), .out1(OUT1[0]), .out2(OUT2[0]));
  _1bit_swap u_1bit_swap_2 (.a(In1[1]), .b(In2[1]), .s(select), .out1(OUT1[1]), .out2(OUT2[1]));
  _1bit_swap u_1bit_swap_3 (.a(In1[2]), .b(In2[2]), .s(select), .out1(OUT1[2]), .out2(OUT2[2]));
  _1bit_swap u_1bit_swap_4 (.a(In1[3]), .b(In2[3]), .s(select), .out1(OUT1[3]), .out2(OUT2[3]));
endmodule

module _4bit_sort (
  input  [3:0] A,
  input  [3:0] B,
  input  [3:0] C,
  input  [3:0] D,
  output [3:0] out_5,
  output [3:0] out_6,
  output [3:0] out_7,
  output [3:0] out_8
);

  wire [3:0] sort_1_out_3, sort_1_out_4, sort_2_out_3, sort_2_out_4, sort_3_out_4, sort_4_out_3;

  sort sort_1 (.in_1(A), .in_2(B), .out_3(sort_1_out_3), .out_4(sort_1_out_4));
  sort sort_2 (.in_1(C), .in_2(D), .out_3(sort_2_out_3), .out_4(sort_2_out_4));
  sort sort_3 (.in_1(sort_1_out_3), .in_2(sort_2_out_3), .out_3(out_5), .out_4(sort_3_out_4));
  sort sort_4 (.in_1(sort_1_out_4), .in_2(sort_2_out_4), .out_3(sort_4_out_3), .out_4(out_8));
  sort sort_5 (.in_1(sort_3_out_4), .in_2(sort_4_out_3), .out_3(out_6), .out_4(out_7));
endmodule

// Sort
module sort (
  input  [3:0] in_1,
  input  [3:0] in_2,
  output [3:0] out_3,
  output [3:0] out_4
);

  wire comparator_1_gt;
  wire [3:0] bit_extender_3_out, bit_extender_4_out;
  wire [4:0] bit_extender_1_out, bit_extender_2_out;

  assign bit_extender_1_out = {{1{1'b0}}, in_1};  // Bit_Extender bit_extender_1
  assign bit_extender_2_out = {{1{1'b0}}, in_2};  // Bit_Extender bit_extender_2
  Bit_Extender #(.in_width(5), .out_width(4)) bit_extender_3 (.in(bit_extender_1_out), .out(bit_extender_3_out));
  Bit_Extender #(.in_width(5), .out_width(4)) bit_extender_4 (.in(bit_extender_2_out), .out(bit_extender_4_out));
  Comparator #(.width(5)) comparator_1 (
    .a(bit_extender_1_out), .b(bit_extender_2_out), .gt(comparator_1_gt));  // open: eq, lt
  _4bit_swap u_4bit_swap_1 (
    .In1(bit_extender_3_out), .In2(bit_extender_4_out), .select(comparator_1_gt), .OUT1(out_3), .OUT2(out_4));
endmodule
