// Logisim project txt.circ as structural Verilog: 2 circuits, main circuit main
module main (
  input  [31:0] N,
  output [31:0] Nth
);

  wire clock_1_out, comp, count_1_out_3, undriven;
  wire [31:0] multiplexer_1_out, Now_q, Pre_q, Sum;

  Multiplexer #(.width(32)) multiplexer_1 (.in0(Sum), .in1(32'h1), .out(multiplexer_1_out), .sel(comp));  // open: en
  Register #(.width(32)) Pre (.D(Now_q), .Q(Pre_q), .clk(clock_1_out), .clr(undriven));  // open: en
  Register #(.width(32)) Now (.D(multiplexer_1_out), .Q(Now_q), .clk(clock_1_out));  // open: en, clr
  Clock clock_1 (.out(clock_1_out));
  Adder #(.width(32)) adder_1 (.a(Pre_q), .b(Now_q), .out(Sum));  // open: cin, cout
  Count count_1 (.in_1(N), .out_3(count_1_out_3));  // open: in_2
  Register #(.width(32)) register_1 (.D(Now_q), .Q(Nth), .clk(count_1_out_3));  // open: en, clr
  Comparator #(.width(32), .mode("unsigned")) comparator_1 (.a(32'h1), .b(Sum), .gt(comp));  // open: eq, lt
endmodule

module Count (
  input  [31:0] in_1,
  input  in_2,
  output out_3
);

  wire clock_1_out, comparator_1_eq, or_1_out;
  wire [31:0] counter_1_q;

  Counter #(.width(32), .max('hffffffff)) counter_1 (
    .Q(counter_1_q), .clk(clock_1_out), .clr(in_2));  // open: load, D, count, carry
  Clock clock_1 (.out(clock_1_out));
  Comparator #(.width(32), .mode("unsigned")) comparator_1 (
    .a(in_1), .b(counter_1_q), .eq(comparator_1_eq));  // open: gt, lt
  Register #(.width(1)) register_1 (.D(or_1_out), .Q(out_3), .clk(clock_1_out));  // open: en, clr
  or or_1 (or_1_out, out_3, comparator_1_eq);
endmodule
